# Fritzing sketch FullArduinoHouse (saved by Fritzing 0.9.5d)
perfboards: 2
stripboards: 4

parts:
  R1 = Resistor [tolerance=±1% resistance=1k package="2512 [SMD]"]
  R2 = Resistor [tolerance=±1% resistance=330 package="2512 [SMD]"]
  U1 = Sharp PC817 [package=THT]
  C1 = Electrolytic Capacitor [capacitance=0.1µF voltage=50V package="100 mil [THT, electrolytic]"]
  ZS-042_RTC1 = ZS-042 RTC Module
  R8 = Resistor [tolerance=±5% resistance=100k package=THT]
  R9 = Resistor [tolerance=±5% resistance=47k package=THT]
  2N3904 = NPN-Transistor [package="TO92 [THT]"]
  R10 = Resistor [tolerance=±5% resistance=100k package=THT]
  R11 = Resistor [tolerance=±5% resistance=10k package=THT]
  R12 = Resistor [tolerance=±5% resistance=10k package=THT]
  J13 = female pin header, 15 pins [form="♀ (female)"]
  Bauteil1 = Arduino Nano 33 IOT
  J14 = female pin header, 15 pins [form="♀ (female)"]
  5V = Voltage Regulator - 5V [package="TO220 [THT]"]
  3_3V = Voltage Regulator - 3.3V [package="TO220 [THT]"]
  ToMosFet = female pin header, 4 pins [form="♀ (female)"]
  MosFet = screw terminal, 6 pins
  J5 = screw terminal, 6 pins
  FanSocket = male pin header, 3 pins [form="♂ (male)"]
  3_3V_2 = male pin header, 2 pins [form="♂ (male)"]
  5V_2 = male pin header, 2 pins [form="♂ (male)"]
  LightDim = male pin header, 2 pins [form="♂ (male)"]
  Moisture = male pin header, 4 pins [form="♂ (male)"]
  LightSwitch = male pin header, 3 pins [form="♂ (male)"]
  SHT31 = male pin header, 5 pins [form="♂ (male)"]
  DS3231 = male pin header, 6 pins [form="♂ (male)"]
  FromMosfet = male pin header, 2 pins [form="♂ (male)"]
  J15 = female pin header, 15 pins [form="♀ (female)"]
  ToMosFet1 = female pin header, 4 pins [form="♀ (female)"]
  J16 = female pin header, 15 pins [form="♀ (female)"]
  R13 = Resistor [tolerance=±5% resistance=10k package=THT]
  R14 = Resistor [tolerance=±5% resistance=10k package=THT]
  R15 = Resistor [tolerance=±5% resistance=47k package=THT]
  2N3905 = NPN-Transistor [package="TO92 [THT]"]
  R16 = Resistor [tolerance=±1% resistance=1k package="2512 [SMD]"]
  R17 = Resistor [tolerance=±1% resistance=330 package="2512 [SMD]"]
  C2 = Electrolytic Capacitor [capacitance=0.1µF voltage=50V package="100 mil [THT, electrolytic]"]
  R18 = Resistor [tolerance=±5% resistance=100k package=THT]
  FanSocket1 = male pin header, 3 pins [form="♂ (male)"]
  3_3V1 = male pin header, 2 pins [form="♂ (male)"]
  5V1 = male pin header, 2 pins [form="♂ (male)"]
  LightDim1 = male pin header, 2 pins [form="♂ (male)"]
  Moisture1 = male pin header, 4 pins [form="♂ (male)"]
  LightSwitch1 = male pin header, 3 pins [form="♂ (male)"]
  SHT32 = male pin header, 5 pins [form="♂ (male)"]
  DS3232 = male pin header, 6 pins [form="♂ (male)"]
  FromMosfet1 = male pin header, 2 pins [form="♂ (male)"]

nets:
  N1: R1.Pin_0, Bauteil1.D4, J14.pin7
  N2: R1.Pin_1, R2.Pin_0, C1.+
  N3: R2.Pin_1, U1.Pin_1, LightDim.pin1
  GND: U1.Pin_2, C1.-, ZS-042_RTC1.GND, 2N3904.E, R10.Pin_1, J13.pin1, J13.pin14, Bauteil1.GND, Bauteil1.D13~, J14.pin4, 5V.GND, 3_3V.GND, ToMosFet.pin1, ToMosFet.pin2, MosFet.pin2, MosFet.pin4, MosFet.pin6, J5.pin6, FanSocket.pin2, 3_3V_2.pin2, 5V_2.pin2, LightDim.pin2, Moisture.pin3, Moisture.pin4, LightSwitch.pin3, SHT31.pin1, DS3231.pin1, FromMosfet.pin2
  N4: U1.Pin_4, R8.Pin_0
  N5: U1.Pin_3, R8.Pin_1
  N6: ZS-042_RTC1.VCC, R11.Pin_0, 3_3V.output_voltage, J5.pin4, 3_3V_2.pin1, Moisture.pin2, LightSwitch.pin1, SHT31.pin2, DS3231.pin2
  N7: ZS-042_RTC1.SDA, J13.pin8, Bauteil1.A4, SHT31.pin4, DS3231.pin4
  N8: ZS-042_RTC1.SCL, J13.pin9, Bauteil1.A5, SHT31.pin3, DS3231.pin3
  N9: ZS-042_RTC1.SQW, Bauteil1.D10~, J14.pin13, DS3231.pin5
  N10: ZS-042_RTC1.32K, DS3231.pin6
  N11: R9.Pin_0, 2N3904.B, R10.Pin_0
  N12: R9.Pin_1, R12.Pin_0, FanSocket.pin1
  N13: 2N3904.C, R11.Pin_1, J13.pin5, Bauteil1.A1
  N14: R12.Pin_1, J13.pin15, Bauteil1.VIN, 5V.output_voltage, MosFet.pin1, MosFet.pin3, FanSocket.pin3, 5V_2.pin1, FromMosfet.pin1
  N15: J13.pin2, Bauteil1.3V3
  N16: J13.pin3, Bauteil1.AREF
  N17: J13.pin4, Bauteil1.A0, Moisture.pin1
  N18: J13.pin6, Bauteil1.A2
  N19: J13.pin7, Bauteil1.A3
  N20: J13.pin10, Bauteil1.A6
  N21: J13.pin11, J13.pin13, Bauteil1.RESET, Bauteil1.A7, J14.pin3
  N22: Bauteil1.RX, J14.pin2
  N23: Bauteil1.TX, J14.pin1
  N24: Bauteil1.D2, J14.pin5, ToMosFet.pin3, ToMosFet.pin4, MosFet.pin5
  N25: Bauteil1.D3~, J14.pin6, J5.pin5, LightSwitch.pin2
  N26: Bauteil1.D5~, J14.pin8
  N27: Bauteil1.D6~, J14.pin9
  N28: Bauteil1.D7, J14.pin10, SHT31.pin5
  N29: Bauteil1.D8, J14.pin11
  N30: Bauteil1.D9~, J14.pin12
  N31: Bauteil1.D11/MOSI, J14.pin14
  N32: Bauteil1.D12~/MISO, J14.pin15
  5V: 5V.input_voltage
  3.3V: 3_3V.input_voltage
  N33: J15.pin5, ToMosFet1.pin3, ToMosFet1.pin4
  N34: J15.pin6, LightSwitch1.pin2
  N35: J15.pin7, R16.Pin_1
  N36: J15.pin10, SHT32.pin5
  N37: J15.pin13, DS3232.pin5
  N38: ToMosFet1.pin1, ToMosFet1.pin2, J16.pin14, 2N3905.E, C2.-, R18.Pin_1, FanSocket1.pin2, 3_3V1.pin2, 5V1.pin2, LightDim1.pin2, Moisture1.pin3, Moisture1.pin4, LightSwitch1.pin3, DS3232.pin1, FromMosfet1.pin2
  N39: J16.pin4, Moisture1.pin1
  N40: J16.pin5, R14.Pin_0, 2N3905.C
  N41: J16.pin8, SHT32.pin4, DS3232.pin4
  N42: J16.pin9, SHT32.pin3, DS3232.pin3
  N43: J16.pin15, 5V1.pin1
  N44: R13.Pin_0, R15.Pin_0, FanSocket1.pin1
  N45: R13.Pin_1, FanSocket1.pin3, FromMosfet1.pin1
  N46: R14.Pin_1, 3_3V1.pin1, SHT32.pin2, DS3232.pin2
  N47: R15.Pin_1, 2N3905.B, R18.Pin_0
  N48: R16.Pin_0, R17.Pin_1, C2.+
  N49: R17.Pin_0, LightDim1.pin1
  N50: Moisture1.pin2, LightSwitch1.pin1

notes:
  TX/RX vertauscht

custom parts:
  Arduino Nano 33 IOT: The Arduino Nano 33 IoT is the easiest and cheapest point of entry to enhance existing devices (and creating new ones) to be part of the IoT and designing pico-network applications. Whether you are looking at building a sensor network connected to your office or home router, or if you want to create a BLE device sending data to a cellphone, the Nano 33 IoT is your one-stop-solution for many of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
